# Fritzing sketch Clock Sketch (saved by Fritzing 0.9.5d)
breadboards: 1

parts:
  part = Arduino Nano (Rev3.0)
  Menu_Button = Pushbutton [package="[SMD]"]
  Button_3 = Pushbutton [package="[SMD]"]
  Button_2 = Pushbutton [package="[SMD]"]
  R3 = Resistor [tolerance=±5% resistance=10000 package="2512 [SMD]"]
  part_2 = Real Time Clock Module - DS1307 RTC Breakout Board
  part_3 = LCD-16X2 [package=lcd-8x2]
  part_4 = BME280 Breakout
  Photoresistor = PHOTOCELL [package=photocell-kit]
  R1 = Resistor [tolerance=±5% resistance=10000 package="2512 [SMD]"]

nets (from the breadboard view):
  GND: part.GND, Button_3.Pin_3, Button_3.Pin_4, Button_2.Pin_3, Button_2.Pin_4, R3.Pin_1, part_2.GND, part_4.GND, R1.Pin_0
  N1: part.D2, Menu_Button.Pin_3, Menu_Button.Pin_4, R1.Pin_1
  N2: part.D3, Button_2.Pin_1, Button_2.Pin_2
  N3: part.D4, Button_3.Pin_1, Button_3.Pin_2
  N4: part.D7, part_3.RS
  N5: part.D8, part_3.DB1
  N6: part.D9, part_3.DB3
  N7: part.D10, part_3.DB5
  N8: part.D11/MOSI, part_3.DB7
  N9: part.D12/MISO, part_3.K
  N10: part.5V, Menu_Button.Pin_1, Menu_Button.Pin_2, part_3.E
  N11: part.A5, part_4.SCK/SCL
  N12: part.A4, part_4.SDI/SDA
  N13: part.A3, R3.Pin_0, Photoresistor.P$1
  N14: part.A1, Photoresistor.P$2
  5V: part_2.5V, part_3.VDD
