# Fritzing sketch touch_sensor_sketch (saved by Fritzing 0.9.5d)
breadboards: 1

parts:
  R1 = Resistor [tolerance=±5% resistance=1000000 package="0603 [SMD]"]
  Metal_Sensor = BUTTON-MAGNETIC [package=Magnetic-snap]
  Part1 = Arduino Nano (Rev3.0)
  LED1 = LEDs [package=led10mm]

nets:
  N1: R1.Pin_0, Part1.D5
  N2: R1.Pin_1, Metal_Sensor.1, Part1.D6
  N3: Part1.A2, LED1.A
